# Fritzing sketch Sketch ARDUINO T5 Esteban Gamarra (saved by Fritzing 0.9.3b)
breadboards: 1

parts:
  Componente1 = Arduino Uno (Rev3)
  LED1 = RGB LED (com. anode, rbg) [package="5 mm [THT]"]
  T1 = LM35 Temperature Sensor [package="TO92 [THT]"]
  R1 = Resistor [tolerance=±5% resistance=220 package="0603 [SMD]"]
  R3 = Resistor [tolerance=±5% resistance=220 package="0603 [SMD]"]
  R4 = Resistor [tolerance=±5% resistance=220 package="0603 [SMD]"]
  Componente2 = Bluetooth HC-05 Macho

nets:
  N1: Componente1.A0, T1.Vout
  GND: Componente1.GND, T1.GND
  N2: Componente1.D3_PWM, Componente2.RXD
  N3: Componente1.D4, R4.Pin_1
  N4: Componente1.D5_PWM, R3.Pin_1
  N5: Componente1.D6_PWM, R1.Pin_1
  N6: Componente1.5V, T1.+Vs
  N7: LED1.red_cathode, R4.Pin_0
  N8: LED1.common_anode, R3.Pin_0
  N9: LED1.green_cathode, R1.Pin_0
